# Fritzing sketch Diegrama Arduino (saved by Fritzing 0.9.3b)
breadboards: 1

parts:
  Componente1 = Arduino Uno (Rev3) - ICSP
  S1 = Round Pushbutton
  R1 = Resistor [tolerance=±5% resistance=330 package=THT]

nets:
  N1: Componente1.GND, R1.Pin_1
  N2: Componente1.D2, S1.leg1, R1.Pin_0
  N3: Componente1.D6_PWM, S1.leg0
